# Fritzing sketch circuit (saved by Fritzing 0.9.3b)

parts:
  Part1 = Adafruit Circuit Playground Dev Edition [part_number="Adafruit #3000"]
  Q1 = NPN-Transistor [package="SOT-23 [SMD]"]
  Q2 = NPN-Transistor [package="SOT-23 [SMD]"]
  part = NPN-Transistor [part_number=PN2222A package="SOT-23 [SMD]"]
  BUTTON1 = Arcade Button (green)
  BUTTON2 = Arcade Button (red)
  BUTTON3 = Arcade Button (blue)
  R1 = Resistor [tolerance=±5% resistance=220 package="0603 [SMD]"]
  R2 = Resistor [tolerance=±5% resistance=220 package="0603 [SMD]"]
  LED5 = Ruby the Red LED
  LED6 = Billie the Blue LED
  LED8 = Gus the Green LED
  LED9 = Gus the Green LED
  LED10 = Gus the Green LED
  LED11 = Billie the Blue LED
  LED12 = Billie the Blue LED
  LED13 = Ruby the Red LED
  LED14 = Ruby the Red LED
  R3 = Resistor [tolerance=±5% resistance=220 package="0603 [SMD]"]
  part_2 = NPN-Transistor [part_number=PN2222A package="SOT-23 [SMD]"]  # not connected
  part_3 = NPN-Transistor [part_number=PN2222A package="SOT-23 [SMD]"]  # not connected

nets:
  N1: Part1.D6, Q1.0
  N2: Part1.GND, Q1.1, Q2.1, part.1, BUTTON1.no_name_yet#1, BUTTON2.no_name_yet#1, BUTTON3.no_name_yet#1
  N3: Part1.D9, part.0
  N4: Part1.D10, Q2.0
  N5: Part1.D0/RX, BUTTON1.no_name_yet#2, R1.Pin_0
  N6: Part1.D2_SDA, BUTTON2.no_name_yet#2, R3.Pin_0
  N7: Part1.D1/TX, BUTTON3.no_name_yet#2, R2.Pin_0
  N8: Part1.VBAT, R1.Pin_1, R2.Pin_1, LED5.anode, LED6.anode, LED8.anode, LED9.anode, LED10.anode, LED11.anode, LED12.anode, LED13.anode, LED14.anode, R3.Pin_1
  N9: Q1.2, LED5.cathode, LED13.cathode, LED14.cathode
  N10: Q2.2, LED6.cathode, LED11.cathode, LED12.cathode
  N11: part.2, LED8.cathode, LED9.cathode, LED10.cathode

custom parts:
  Adafruit Circuit Playground Dev Edition: Would you like to learn electronics, with an all-in-one board that has sensors and LEDs built in? Circuit Playground is here - and it's the best way to practice programming on real hardware with no soldering or sewing required! Circuit Playground features an ATmega32u4 processor, just like our popular Flora. The board's also round and has alligator-clip pads around it so you don't have to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
  Arcade Button (green): Adafruit Arcade Button (green)
  Arcade Button (red): Adafruit Arcade Button (red)
  Arcade Button (blue): Adafruit Arcade Button (blue)
